# Fritzing sketch UserPortGpios (saved by Fritzing 0.9.3b)
circuit board: 7.55415cm x 5.66325cm
breadboards: 1

parts:
  Q1 = NPN-Transistor [package="TO92 [THT]"]
  R2 = Resistor [tolerance=±5% resistance=220 package=THT]
  LED1 = LED - 5mm [color="Red (633nm)" package="5 mm [THT]"]
  Q2 = NPN-Transistor [package="TO92 [THT]"]
  R3 = Resistor [tolerance=±5% resistance=220 package=THT]
  LED2 = LED - 5mm [color="Red (633nm)" package="5 mm [THT]"]
  Q3 = NPN-Transistor [package="TO92 [THT]"]
  R4 = Resistor [tolerance=±5% resistance=220 package=THT]
  LED3 = LED - 5mm [color="Red (633nm)" package="5 mm [THT]"]
  Q4 = NPN-Transistor [package="TO92 [THT]"]
  R5 = Resistor [tolerance=±5% resistance=220 package=THT]
  LED4 = LED - 5mm [color="Red (633nm)" package="5 mm [THT]"]
  Q5 = NPN-Transistor [package="TO92 [THT]"]
  R6 = Resistor [tolerance=±5% resistance=220 package=THT]
  LED5 = LED - 5mm [color="Red (633nm)" package="5 mm [THT]"]
  Q6 = NPN-Transistor [package="TO92 [THT]"]
  R7 = Resistor [tolerance=±5% resistance=220 package=THT]
  LED6 = LED - 5mm [color="Red (633nm)" package="5 mm [THT]"]
  Q7 = NPN-Transistor [package="TO92 [THT]"]
  R8 = Resistor [tolerance=±5% resistance=220 package=THT]
  LED7 = LED - 5mm [color="Red (633nm)" package="5 mm [THT]"]
  Q8 = NPN-Transistor [package="TO92 [THT]"]
  R9 = Resistor [tolerance=±5% resistance=220 package=THT]
  LED8 = LED - 5mm [color="Red (633nm)" package="5 mm [THT]"]
  R10 = Resistor [tolerance=±5% resistance=220 package=THT]
  R11 = Resistor [tolerance=±5% resistance=220 package=THT]
  R12 = Resistor [tolerance=±5% resistance=220 package=THT]
  R13 = Resistor [tolerance=±5% resistance=220 package=THT]
  R14 = Resistor [tolerance=±5% resistance=220 package=THT]
  R15 = Resistor [tolerance=±5% resistance=220 package=THT]
  R16 = Resistor [tolerance=±5% resistance=220 package=THT]
  R17 = Resistor [tolerance=±5% resistance=220 package=THT]
  Pad1 = Pad [width=1.6788703361305291 height=5.6668226620046536 connect=center]  # not connected
  Pad2 = Pad [width=1.6788703361305291 height=5.6668226620046536 connect=center]
  Pad3 = Pad [width=1.6788703361305291 height=5.6668226620046536 connect=center]  # not connected
  Pad4 = Pad [width=1.6788703361305291 height=5.6668226620046536 connect=center]  # not connected
  Pad5 = Pad [width=1.6788703361305291 height=5.6668226620046536 connect=center]  # not connected
  Pad6 = Pad [width=1.6788703361305291 height=5.6668226620046536 connect=center]
  Pad7 = Pad [width=1.6788703361305291 height=5.6668226620046536 connect=center]
  Pad8 = Pad [width=1.6788703361305291 height=5.6668226620046536 connect=center]
  Pad9 = Pad [width=1.6788703361305291 height=5.6668226620046536 connect=center]
  Pad10 = Pad [width=1.6788703361305291 height=5.6668226620046536 connect=center]  # not connected
  Pad11 = Pad [width=1.6788703361305291 height=5.6668226620046536 connect=center]  # not connected
  Pad12 = Pad [width=1.6788703361305291 height=5.6668226620046536 connect=center]
  Pad17 = Pad [width=1.6788703361305291 height=5.6668226620046536 connect=center]
  Pad15 = Pad [width=1.6788703361305291 height=5.6668226620046536 connect=center]  # not connected
  Pad23 = Pad [width=1.6788703361305291 height=5.6668226620046536 connect=center]
  Pad14 = Pad [width=1.6788703361305291 height=5.6668226620046536 connect=center]  # not connected
  Pad22 = Pad [width=1.6788703361305291 height=5.6668226620046536 connect=center]  # not connected
  Pad16 = Pad [width=1.6788703361305291 height=5.6668226620046536 connect=center]  # not connected
  Pad24 = Pad [width=1.6788703361305291 height=5.6668226620046536 connect=center]
  Pad19 = Pad [width=1.6788703361305291 height=5.6668226620046536 connect=center]  # not connected
  Pad21 = Pad [width=1.6788703361305291 height=5.6668226620046536 connect=center]
  Pad20 = Pad [width=1.6788703361305291 height=5.6668226620046536 connect=center]
  Pad18 = Pad [width=1.6788703361305291 height=5.6668226620046536 connect=center]  # not connected
  Pad13 = Pad [width=1.6788703361305291 height=5.6668226620046536 connect=center]  # not connected

nets:
  N1: Q1.E, R17.Pin_1
  N2: Q1.B, R2.Pin_0
  5V: Q1.C, Q2.C, Q3.C, Q4.C, Q5.C, Q6.C, Q7.C, Q8.C, Pad2.pad
  N3: R2.Pin_1, Pad23.pad
  GND: LED1.cathode, LED2.cathode, LED3.cathode, LED4.cathode, LED5.cathode, LED6.cathode, LED7.cathode, LED8.cathode, Pad12.pad, Pad17.pad
  N4: LED1.anode, R17.Pin_0
  N5: Q2.E, R10.Pin_1
  N6: Q2.B, R3.Pin_0
  N7: R3.Pin_1, Pad20.pad
  N8: LED2.anode, R10.Pin_0
  N9: Q3.E, R11.Pin_1
  N10: Q3.B, R4.Pin_0
  N11: R4.Pin_1, Pad9.pad
  N12: LED3.anode, R11.Pin_0
  N13: Q4.E, R12.Pin_1
  N14: Q4.B, R5.Pin_0
  N15: R5.Pin_1, Pad8.pad
  N16: LED4.anode, R12.Pin_0
  N17: Q5.E, R13.Pin_1
  N18: Q5.B, R6.Pin_0
  N19: R6.Pin_1, Pad7.pad
  N20: LED5.anode, R13.Pin_0
  N21: Q6.E, R14.Pin_1
  N22: Q6.B, R7.Pin_0
  N23: R7.Pin_1, Pad6.pad
  N24: LED6.anode, R14.Pin_0
  N25: Q7.E, R15.Pin_1
  N26: Q7.B, R8.Pin_0
  N27: R8.Pin_1, Pad21.pad
  N28: LED7.anode, R15.Pin_0
  N29: Q8.E, R16.Pin_1
  N30: Q8.B, R9.Pin_0
  N31: R9.Pin_1, Pad24.pad
  N32: LED8.anode, R16.Pin_0

notes:
  12
  1
  P0 (B)
  P1 (K)
  P2 (4)
  P3 (5)
  P4 (6)
  P5 (7)
  P6 (J)
  P7 (F)
  2
  3
  4
  5
  6
  7
  8
  9
  10
  11
